# Fritzing sketch layout (saved by Fritzing 0.8.5b)
breadboards: 1

parts:
  Raspberry_Pi_B_rev1 = Raspberry Pi B rev2
  R1 = Resistor [tolerance=±5% resistance=470 package=THT]
  LED1 = smd LED [color="Red (633nm)" package="0603 [SMD]"]

nets:
  N1: Raspberry_Pi_B_rev1.GND, R1.Pin_1
  N2: Raspberry_Pi_B_rev1.GPIO_18, LED1.cathode
  N3: R1.Pin_0, LED1.anode
